# Fritzing sketch bufsm (saved by Fritzing 0.9.3b)
breadboards: 1

parts:
  Part1 = Arduino Nano (Rev3.0)
  R1 = Resistor [tolerance=±5% resistance=330 package="2010 [SMD]"]
  A7_Module_v2 = QFN-24 [chip_label=QFN-24 package=QFN]
  LED1 = RGB LED (com. cathode, rgb) [package="5 mm [THT]"]
  R2 = Resistor [tolerance=±5% resistance=10k package="2010 [SMD]"]
  R3 = Resistor [tolerance=±5% resistance=10k package="2010 [SMD]"]
  R4 = Resistor [tolerance=±5% resistance=10k package="2010 [SMD]"]
  R5 = Resistor [tolerance=±5% resistance=10k package="2010 [SMD]"]
  Q1 = TRANSISTOR_NPN [part_number=2N3904 package=to-92-ammo]
  R6 = Resistor [tolerance=±5% resistance=330 package="2010 [SMD]"]
  R7 = Resistor [tolerance=±5% resistance=10k package="2010 [SMD]"]
  R8 = Resistor [tolerance=±5% resistance=330 package="2010 [SMD]"]
  LED2 = RGB LED (com. cathode, rgb) [package="5 mm [THT]"]
  C1 = Electrolytic Capacitor [package="100 mil [THT, electrolytic]"]

nets:
  uC_URXD: Part1.D1/TX, R2.Pin_1
  UTXD_uC: Part1.D0/RX, A7_Module_v2.8
  GND: Part1.GND, R1.Pin_0, A7_Module_v2.2, A7_Module_v2.14, R3.Pin_0, R5.Pin_0, Q1.E, R8.Pin_0, C1.-
  GPS_uC: Part1.D2, A7_Module_v2.24
  uC_RD1: Part1.D3, LED1.red_anode
  uC_BL1: Part1.D4, LED1.blue_anode
  uC_GR1: Part1.D5, LED1.green_anode
  uC_RST: Part1.D6, R6.Pin_0
  uC_PWR: Part1.D7, R4.Pin_1
  uC_RD2: Part1.D8, LED2.red_anode
  uC_BL2: Part1.D9, LED2.blue_anode
  uC_GR2: Part1.D10, LED2.green_anode
  5V: Part1.5V
  3.3V: Part1.3V3, R7.Pin_1
  N1: R1.Pin_1, LED1.common_cathode
  N2: A7_Module_v2.1, C1.+
  N3: A7_Module_v2.9, R2.Pin_0, R3.Pin_1
  N4: A7_Module_v2.13, R4.Pin_0, R5.Pin_1
  RST_A7: A7_Module_v2.19, Q1.C, R7.Pin_0
  N5: Q1.B, R6.Pin_1
  N6: R8.Pin_1, LED2.common_cathode

custom parts:
  Electrolytic Capacitor: A small electrolytic capacitor
